// Logisim project Project3-2.circ as structural Verilog: 23 circuits, main circuit main
module main (
);

  wire clock_2_out, cpu_1_data_write_e, cpu_1_mem_write_e, keyboard_1_avail,
       keyboardcontroller_1_databuswrite, keyboardcontroller_1_keyboardread, memory_1_data_bus_write_e,
       rgb_video_1_p1, rgb_video_1_p2;
  wire [5:0] rgb_video_1_p3, rgb_video_1_p4;
  wire [6:0] keyboard_1_data;
  wire [15:0] cpu_1_address;
  wire [23:0] rgb_video_1_p5;
  wire [31:0] controlled_buffer_1_out, cpu_1_data_bus, keyboardcontroller_1_databusout, memory_1_data_bus_out;

  // RGB_Video #(.height(64), .scale(4), .width(64)) rgb_video_1: pin names not known; wires that end beside it: rgb_video_1_p1, rgb_video_1_p2, rgb_video_1_p3, rgb_video_1_p4, rgb_video_1_p5
  Clock clock_1 (.out(rgb_video_1_p1));
  Clock clock_2 (.out(clock_2_out));
  Keyboard keyboard_1 (
    .clk(clock_2_out), .re(keyboardcontroller_1_keyboardread), .avail(keyboard_1_avail),
    .data(keyboard_1_data));  // open: clr
  assign controlled_buffer_1_out = memory_1_data_bus_write_e ? memory_1_data_bus_out : 32'bz;  // Controlled_Buffer controlled_buffer_1
  Memory memory_1 (
    .Write_e(cpu_1_mem_write_e), .Address(cpu_1_address), .Data_Bus_in(controlled_buffer_1_out),
    .Data_Bus_out(memory_1_data_bus_out), .Data_Bus_Write_e(memory_1_data_bus_write_e));
  assign controlled_buffer_1_out = cpu_1_data_write_e ? cpu_1_data_bus : 32'bz;  // Controlled_Buffer controlled_buffer_2
  CPU cpu_1 (
    .Data_bus_in(controlled_buffer_1_out), .Data_bus(cpu_1_data_bus), .Data_write_e(cpu_1_data_write_e),
    .Address(cpu_1_address), .Mem_write_e(cpu_1_mem_write_e));
  assign controlled_buffer_1_out = keyboardcontroller_1_databuswrite ? keyboardcontroller_1_databusout : 32'bz;  // Controlled_Buffer controlled_buffer_3
  KeyboardController keyboardcontroller_1 (
    .DataBusIn(controlled_buffer_1_out), .WriteEnable(cpu_1_mem_write_e), .AddressIn(cpu_1_address),
    .KeyboardIn(keyboard_1_data), .KeyboardKeyPressAvailable(keyboard_1_avail),
    .DataBusOut(keyboardcontroller_1_databusout), .DataBusWrite(keyboardcontroller_1_databuswrite),
    .KeyboardRead(keyboardcontroller_1_keyboardread));
  RGBController rgbcontroller_1 (
    .AddressIn(cpu_1_address), .DataBusIn(controlled_buffer_1_out), .WriteEnable(cpu_1_mem_write_e),
    .RGBX(rgb_video_1_p3), .RGBY(rgb_video_1_p4), .RGBColor(rgb_video_1_p5), .RGBWrite(rgb_video_1_p2));
endmodule

module regfile (
  input  we,
  input  [4:0] rdselect,
  input  [31:0] rd,
  input  [4:0] rsselect,
  input  [4:0] rtselect,
  output [31:0] rt,
  output [31:0] rs
);

  wire clock_1_out, demultiplexer_1_out1, demultiplexer_1_out2, demultiplexer_1_out3, demultiplexer_1_out4,
       demultiplexer_1_out5, demultiplexer_1_out6, demultiplexer_1_out7, demultiplexer_1_out8,
       demultiplexer_1_out9, demultiplexer_1_out10, demultiplexer_1_out11, demultiplexer_1_out12,
       demultiplexer_1_out13, demultiplexer_1_out14, demultiplexer_1_out15, demultiplexer_1_out16,
       demultiplexer_1_out17, demultiplexer_1_out18, demultiplexer_1_out19, demultiplexer_1_out20,
       demultiplexer_1_out21, demultiplexer_1_out22, demultiplexer_1_out23, demultiplexer_1_out24,
       demultiplexer_1_out25, demultiplexer_1_out26, demultiplexer_1_out27, demultiplexer_1_out28,
       demultiplexer_1_out29, demultiplexer_1_out30, demultiplexer_1_out31;
  wire [31:0] Reg1_q, Reg2_q, Reg3_q, Reg4_q, Reg5_q, Reg6_q, Reg7_q, Reg8_q, Reg9_q, Reg10_q, Reg11_q,
       Reg12_q, Reg13_q, Reg14_q, Reg15_q, Reg16_q, Reg17_q, Reg18_q, Reg19_q, Reg20_q, Reg21_q, Reg22_q,
       Reg23_q, Reg24_q, Reg25_q, Reg26_q, Reg27_q, Reg28_q, Reg29_q, Reg30_q, Reg31_q;

  Clock clock_1 (.out(clock_1_out));
  Demultiplexer #(.enable("false"), .select(5)) demultiplexer_1 (
    .out1(demultiplexer_1_out1), .out2(demultiplexer_1_out2), .out3(demultiplexer_1_out3),
    .out4(demultiplexer_1_out4), .out5(demultiplexer_1_out5), .out6(demultiplexer_1_out6),
    .out7(demultiplexer_1_out7), .out8(demultiplexer_1_out8), .out9(demultiplexer_1_out9),
    .out10(demultiplexer_1_out10), .out11(demultiplexer_1_out11), .out12(demultiplexer_1_out12),
    .out13(demultiplexer_1_out13), .out14(demultiplexer_1_out14), .out15(demultiplexer_1_out15),
    .out16(demultiplexer_1_out16), .out17(demultiplexer_1_out17), .out18(demultiplexer_1_out18),
    .out19(demultiplexer_1_out19), .out20(demultiplexer_1_out20), .out21(demultiplexer_1_out21),
    .out22(demultiplexer_1_out22), .out23(demultiplexer_1_out23), .out24(demultiplexer_1_out24),
    .out25(demultiplexer_1_out25), .out26(demultiplexer_1_out26), .out27(demultiplexer_1_out27),
    .out28(demultiplexer_1_out28), .out29(demultiplexer_1_out29), .out30(demultiplexer_1_out30),
    .out31(demultiplexer_1_out31), .in(we), .sel(rdselect));  // open: out0
  Register #(.width(32)) Reg1 (.D(rd), .en(demultiplexer_1_out1), .clk(clock_1_out), .Q(Reg1_q));  // open: clr
  Register #(.width(32)) Reg2 (.D(rd), .en(demultiplexer_1_out2), .clk(clock_1_out), .Q(Reg2_q));  // open: clr
  Register #(.width(32)) Reg3 (.D(rd), .en(demultiplexer_1_out3), .clk(clock_1_out), .Q(Reg3_q));  // open: clr
  Register #(.width(32)) Reg4 (.D(rd), .en(demultiplexer_1_out4), .clk(clock_1_out), .Q(Reg4_q));  // open: clr
  Register #(.width(32)) Reg5 (.D(rd), .en(demultiplexer_1_out5), .clk(clock_1_out), .Q(Reg5_q));  // open: clr
  Register #(.width(32)) Reg6 (.D(rd), .en(demultiplexer_1_out6), .clk(clock_1_out), .Q(Reg6_q));  // open: clr
  Register #(.width(32)) Reg7 (.D(rd), .en(demultiplexer_1_out7), .clk(clock_1_out), .Q(Reg7_q));  // open: clr
  Register #(.width(32)) Reg8 (.D(rd), .en(demultiplexer_1_out8), .clk(clock_1_out), .Q(Reg8_q));  // open: clr
  Register #(.width(32)) Reg9 (.D(rd), .en(demultiplexer_1_out9), .clk(clock_1_out), .Q(Reg9_q));  // open: clr
  Register #(.width(32)) Reg10 (.D(rd), .en(demultiplexer_1_out10), .clk(clock_1_out), .Q(Reg10_q));  // open: clr
  Register #(.width(32)) Reg11 (.D(rd), .en(demultiplexer_1_out11), .clk(clock_1_out), .Q(Reg11_q));  // open: clr
  Register #(.width(32)) Reg12 (.D(rd), .en(demultiplexer_1_out12), .clk(clock_1_out), .Q(Reg12_q));  // open: clr
  Register #(.width(32)) Reg13 (.D(rd), .en(demultiplexer_1_out13), .clk(clock_1_out), .Q(Reg13_q));  // open: clr
  Register #(.width(32)) Reg14 (.D(rd), .en(demultiplexer_1_out14), .clk(clock_1_out), .Q(Reg14_q));  // open: clr
  Register #(.width(32)) Reg15 (.D(rd), .en(demultiplexer_1_out15), .clk(clock_1_out), .Q(Reg15_q));  // open: clr
  Register #(.width(32)) Reg16 (.D(rd), .en(demultiplexer_1_out16), .clk(clock_1_out), .Q(Reg16_q));  // open: clr
  Register #(.width(32)) Reg17 (.D(rd), .en(demultiplexer_1_out17), .clk(clock_1_out), .Q(Reg17_q));  // open: clr
  Register #(.width(32)) Reg18 (.D(rd), .en(demultiplexer_1_out18), .clk(clock_1_out), .Q(Reg18_q));  // open: clr
  Register #(.width(32)) Reg19 (.D(rd), .en(demultiplexer_1_out19), .clk(clock_1_out), .Q(Reg19_q));  // open: clr
  Register #(.width(32)) Reg20 (.D(rd), .en(demultiplexer_1_out20), .clk(clock_1_out), .Q(Reg20_q));  // open: clr
  Register #(.width(32)) Reg21 (.D(rd), .en(demultiplexer_1_out21), .clk(clock_1_out), .Q(Reg21_q));  // open: clr
  Register #(.width(32)) Reg22 (.D(rd), .en(demultiplexer_1_out22), .clk(clock_1_out), .Q(Reg22_q));  // open: clr
  Register #(.width(32)) Reg23 (.D(rd), .en(demultiplexer_1_out23), .clk(clock_1_out), .Q(Reg23_q));  // open: clr
  Register #(.width(32)) Reg24 (.D(rd), .en(demultiplexer_1_out24), .clk(clock_1_out), .Q(Reg24_q));  // open: clr
  Register #(.width(32)) Reg25 (.D(rd), .en(demultiplexer_1_out25), .clk(clock_1_out), .Q(Reg25_q));  // open: clr
  Register #(.width(32)) Reg26 (.D(rd), .en(demultiplexer_1_out26), .clk(clock_1_out), .Q(Reg26_q));  // open: clr
  Register #(.width(32)) Reg27 (.D(rd), .en(demultiplexer_1_out27), .clk(clock_1_out), .Q(Reg27_q));  // open: clr
  Register #(.width(32)) Reg28 (.D(rd), .en(demultiplexer_1_out28), .clk(clock_1_out), .Q(Reg28_q));  // open: clr
  Register #(.width(32)) Reg29 (.D(rd), .en(demultiplexer_1_out29), .clk(clock_1_out), .Q(Reg29_q));  // open: clr
  Register #(.width(32)) Reg30 (.D(rd), .en(demultiplexer_1_out30), .clk(clock_1_out), .Q(Reg30_q));  // open: clr
  Register #(.width(32)) Reg31 (.D(rd), .en(demultiplexer_1_out31), .clk(clock_1_out), .Q(Reg31_q));  // open: clr
  Multiplexer #(.enable("false"), .select(5), .width(32)) multiplexer_1 (
    .in0({32{1'b0}}), .in1(Reg1_q), .in2(Reg2_q), .in3(Reg3_q), .in4(Reg4_q), .in5(Reg5_q), .in6(Reg6_q),
    .in7(Reg7_q), .in8(Reg8_q), .in9(Reg9_q), .in10(Reg10_q), .in11(Reg11_q), .in12(Reg12_q), .in13(Reg13_q),
    .in14(Reg14_q), .in15(Reg15_q), .in16(Reg16_q), .in17(Reg17_q), .in18(Reg18_q), .in19(Reg19_q),
    .in20(Reg20_q), .in21(Reg21_q), .in22(Reg22_q), .in23(Reg23_q), .in24(Reg24_q), .in25(Reg25_q),
    .in26(Reg26_q), .in27(Reg27_q), .in28(Reg28_q), .in29(Reg29_q), .in30(Reg30_q), .in31(Reg31_q), .out(rs),
    .sel(rsselect));
  Multiplexer #(.enable("false"), .select(5), .width(32)) multiplexer_2 (
    .in0({32{1'b0}}), .in1(Reg1_q), .in2(Reg2_q), .in3(Reg3_q), .in4(Reg4_q), .in5(Reg5_q), .in6(Reg6_q),
    .in7(Reg7_q), .in8(Reg8_q), .in9(Reg9_q), .in10(Reg10_q), .in11(Reg11_q), .in12(Reg12_q), .in13(Reg13_q),
    .in14(Reg14_q), .in15(Reg15_q), .in16(Reg16_q), .in17(Reg17_q), .in18(Reg18_q), .in19(Reg19_q),
    .in20(Reg20_q), .in21(Reg21_q), .in22(Reg22_q), .in23(Reg23_q), .in24(Reg24_q), .in25(Reg25_q),
    .in26(Reg26_q), .in27(Reg27_q), .in28(Reg28_q), .in29(Reg29_q), .in30(Reg30_q), .in31(Reg31_q), .out(rt),
    .sel(rtselect));

  // Notes on the sheet:
  //   Reg0
  //   rsselect Multiplex
  //   rtselect Multiplex
endmodule

module ALU (
  input  [4:0] arith_code,
  input  [31:0] IN1,
  input  [31:0] IN2,
  input  [4:0] shift_amt,
  output isRegEqual,
  output [31:0] outval
);

  wire clock_1_out, clock_2_out, comparator_2_lt, multiplexer_3_out;
  wire [31:0] adder_1_out, and_1_out, bit_extender_1_out, divider_1_out, divider_1_rem, HI_q, LO_q,
       multiplexer_1_out, multiplexer_2_out, multiplier_1_cout, multiplier_1_out, nor_1_out, or_1_out,
       shifter_1_out, shifter_2_out, subtractor_1_out, xor_1_out;

  Comparator #(.width(32)) comparator_1 (.a(IN1), .b(IN2), .eq(isRegEqual));  // open: gt, lt
  Divider #(.width(32)) divider_1 (.a(IN1), .b(IN2), .out(divider_1_out), .rem(divider_1_rem));  // open: upper
  Shifter #(.width(32)) shifter_1 (.in(IN1), .\dist (shift_amt), .out(shifter_1_out));
  Shifter #(.shift("lr"), .width(32)) shifter_2 (.in(IN1), .\dist (shift_amt), .out(shifter_2_out));
  Comparator #(.width(32)) comparator_2 (.a(IN1), .b(IN2), .lt(comparator_2_lt));  // open: gt, eq
  Adder #(.width(32)) adder_1 (.a(IN1), .b(IN2), .out(adder_1_out));  // open: cin, cout
  Subtractor #(.width(32)) subtractor_1 (.a(IN1), .b(IN2), .out(subtractor_1_out));  // open: bin, bout
  Multiplier #(.width(32)) multiplier_1 (
    .a(IN1), .b(IN2), .out(multiplier_1_out), .cout(multiplier_1_cout));  // open: cin
  assign bit_extender_1_out = {{31{1'b0}}, comparator_2_lt};  // Bit_Extender bit_extender_1
  assign and_1_out = IN1 & IN2;  // AND_Gate and_1, 32 bits wide
  assign or_1_out = IN1 | IN2;  // OR_Gate or_1, 32 bits wide
  assign nor_1_out = ~(IN1 | IN2);  // NOR_Gate nor_1, 32 bits wide
  assign xor_1_out = IN1 ^ IN2;  // XOR_Gate xor_1, 32 bits wide
  Multiplexer #(.enable("false"), .select(5), .width(32)) multiplexer_1 (
    .in3(multiplier_1_cout), .in4(divider_1_rem), .out(multiplexer_1_out), .sel(arith_code));  // open: in0, in1, in2, in5, in6, in7, in8, in9, in10, in11, in12, in13, in14, in15, in16, in17, in18, in19, in20, in21, in22, in23, in24, in25, in26, in27, in28, in29, in30, in31
  Multiplexer #(.enable("false"), .select(5), .width(32)) multiplexer_2 (
    .in3(multiplier_1_out), .in4(divider_1_out), .out(multiplexer_2_out), .sel(arith_code));  // open: in0, in1, in2, in5, in6, in7, in8, in9, in10, in11, in12, in13, in14, in15, in16, in17, in18, in19, in20, in21, in22, in23, in24, in25, in26, in27, in28, in29, in30, in31
  Multiplexer #(.enable("false"), .select(5)) multiplexer_3 (
    .in0(1'b0), .in1(1'b0), .in2(1'b0), .in3(1'b1), .in4(1'b1), .in5(1'b0), .in6(1'b0), .in7(1'b0),
    .in8(1'b0), .in9(1'b0), .in10(1'b0), .in11(1'b0), .in12(1'b0), .in13(1'b0), .in14(1'b0), .in15(1'b0),
    .in16(1'b0), .in17(1'b0), .in18(1'b0), .in19(1'b0), .in20(1'b0), .in21(1'b0), .in22(1'b0), .in23(1'b0),
    .in24(1'b0), .in25(1'b0), .in26(1'b0), .in27(1'b0), .in28(1'b0), .in29(1'b0), .in30(1'b0), .in31(1'b0),
    .out(multiplexer_3_out), .sel(arith_code));
  Register #(.width(32)) HI (.D(multiplexer_1_out), .en(multiplexer_3_out), .clk(clock_1_out), .Q(HI_q));  // open: clr
  Clock clock_1 (.out(clock_1_out));
  Register #(.width(32)) LO (.D(multiplexer_2_out), .en(multiplexer_3_out), .clk(clock_2_out), .Q(LO_q));  // open: clr
  Clock clock_2 (.out(clock_2_out));
  Multiplexer #(.enable("false"), .select(5), .width(32)) multiplexer_4 (
    .in0(32'hfefab), .in1(adder_1_out), .in2(subtractor_1_out), .in3(32'hfefab), .in4(32'hfefab), .in5(HI_q),
    .in6(LO_q), .in7(32'hfefab), .in8(bit_extender_1_out), .in9(shifter_1_out), .in10(shifter_2_out),
    .in11(and_1_out), .in12(or_1_out), .in13(nor_1_out), .in14(xor_1_out), .in15(32'hfefab),
    .in16(32'hfefab), .in17(32'hfefab), .in18(32'hfefab), .in19(32'hfefab), .in20(32'hfefab),
    .in21(32'hfefab), .in22(32'hfefab), .in23(32'hfefab), .in24(32'hfefab), .in25(32'hfefab),
    .in26(32'hfefab), .in27(32'hfefab), .in28(32'hfefab), .in29(32'hfefab), .in30(32'hfefab),
    .in31(32'hfefab), .out(outval), .sel(arith_code));

  // Notes on the sheet:
  //   top multiplexer writes to out, middle multiplexer to HI, third multiplexer writes to lo, last multiplexer writes to write_enable for HI/LO
endmodule

module getimm (
  input  [31:0] Instruction,
  output [15:0] immediate
);


  assign immediate = Instruction[15:0];
endmodule

module getimmselect (
  input  [31:0] instruction,
  output imm_select
);

  wire and_1_out, comparator_1_eq, multiplexer_1_out, multiplexer_2_out, multiplexer_3_out,
       multiplexer_4_out, multiplexer_5_out, multiplexer_6_out;

  Multiplexer #(.enable("false"), .select(5)) multiplexer_1 (
    .in0(1'b0), .in1(1'b0), .in2(1'b0), .in3(1'b0), .in4(1'b0), .in5(1'b0), .in6(1'b0), .in7(1'b0),
    .in8(1'b1), .in9(1'b0), .in10(1'b0), .in11(1'b0), .in12(1'b1), .in13(1'b1), .in14(1'b1), .in15(1'b0),
    .in16(1'b0), .in17(1'b0), .in18(1'b0), .in19(1'b0), .in20(1'b0), .in21(1'b0), .in22(1'b0), .in23(1'b0),
    .in24(1'b0), .in25(1'b0), .in26(1'b0), .in27(1'b0), .in28(1'b0), .in29(1'b0), .in30(1'b0), .in31(1'b0),
    .out(multiplexer_1_out), .sel(instruction[30:26]));
  Multiplexer #(.enable("false"), .select(5)) multiplexer_2 (
    .in0(1'b0), .in1(1'b0), .in2(1'b0), .in3(1'b1), .in4(1'b0), .in5(1'b0), .in6(1'b0), .in7(1'b0),
    .in8(1'b0), .in9(1'b0), .in10(1'b0), .in11(1'b1), .in12(1'b0), .in13(1'b0), .in14(1'b0), .in15(1'b0),
    .in16(1'b0), .in17(1'b0), .in18(1'b0), .in19(1'b0), .in20(1'b0), .in21(1'b0), .in22(1'b0), .in23(1'b0),
    .in24(1'b0), .in25(1'b0), .in26(1'b0), .in27(1'b0), .in28(1'b0), .in29(1'b0), .in30(1'b0), .in31(1'b0),
    .out(multiplexer_2_out), .sel(instruction[30:26]));
  Comparator #(.width(6)) comparator_1 (.a({6{1'b0}}), .b(instruction[31:26]), .eq(comparator_1_eq));  // open: gt, lt
  Multiplexer #(.enable("false")) multiplexer_3 (
    .in0(multiplexer_1_out), .in1(multiplexer_2_out), .out(multiplexer_3_out), .sel(instruction[31]));
  Multiplexer #(.enable("false"), .select(5)) multiplexer_4 (
    .in0(1'b0), .in1(1'b0), .in2(1'b0), .in3(1'b0), .in4(1'b0), .in5(1'b0), .in6(1'b0), .in7(1'b0),
    .in8(1'b0), .in9(1'b0), .in10(1'b0), .in11(1'b0), .in12(1'b0), .in13(1'b0), .in14(1'b0), .in15(1'b0),
    .in16(1'b0), .in17(1'b0), .in18(1'b0), .in19(1'b0), .in20(1'b0), .in21(1'b0), .in22(1'b0), .in23(1'b0),
    .in24(1'b0), .in25(1'b0), .in26(1'b0), .in27(1'b0), .in28(1'b0), .in29(1'b0), .in30(1'b0), .in31(1'b0),
    .out(multiplexer_4_out), .sel(instruction[4:0]));
  Multiplexer #(.enable("false"), .select(5)) multiplexer_5 (
    .in0(1'b0), .in1(1'b0), .in2(1'b0), .in3(1'b0), .in4(1'b0), .in5(1'b0), .in6(1'b0), .in7(1'b0),
    .in8(1'b0), .in9(1'b0), .in10(1'b0), .in11(1'b0), .in12(1'b0), .in13(1'b0), .in14(1'b0), .in15(1'b0),
    .in16(1'b0), .in17(1'b0), .in18(1'b0), .in19(1'b0), .in20(1'b0), .in21(1'b0), .in22(1'b0), .in23(1'b0),
    .in24(1'b0), .in25(1'b0), .in26(1'b0), .in27(1'b0), .in28(1'b0), .in29(1'b0), .in30(1'b0), .in31(1'b0),
    .out(multiplexer_5_out), .sel(instruction[4:0]));
  Multiplexer #(.enable("false")) multiplexer_6 (
    .in0(multiplexer_4_out), .in1(multiplexer_5_out), .out(multiplexer_6_out), .sel(instruction[5]));
  and and_1 (and_1_out, multiplexer_6_out, comparator_1_eq);
  or or_1 (imm_select, multiplexer_3_out, and_1_out);

  // Notes on the sheet:
  //   for the imm_select to be 1, we need to be doing an addi
endmodule

module getshtamt (
  input  [31:0] Instruction,
  output [4:0] shiftamt
);


  assign shiftamt = Instruction[10:6];
endmodule

module getaluselect (
  input  [31:0] Instruction,
  output [4:0] alu_select
);

  wire getimmselect_1_imm_select;
  wire [4:0] multiplexer_1_out, multiplexer_2_out, multiplexer_3_out, multiplexer_4_out, multiplexer_5_out,
       multiplexer_6_out;

  Multiplexer #(.enable("false"), .select(5), .width(5)) multiplexer_1 (
    .in0(5'b01001), .in1({5{1'b0}}), .in2(5'b01010), .in3({5{1'b0}}), .in4({5{1'b0}}), .in5({5{1'b0}}),
    .in6({5{1'b0}}), .in7({5{1'b0}}), .in8({5{1'b0}}), .in9({5{1'b0}}), .in10({5{1'b0}}), .in11({5{1'b0}}),
    .in12({5{1'b0}}), .in13({5{1'b0}}), .in14({5{1'b0}}), .in15({5{1'b0}}), .in16(5'b00101),
    .in17({5{1'b0}}), .in18(5'b00110), .in19({5{1'b0}}), .in20({5{1'b0}}), .in21({5{1'b0}}),
    .in22({5{1'b0}}), .in23({5{1'b0}}), .in24(5'b00011), .in25({5{1'b0}}), .in26(5'b00100), .in27({5{1'b0}}),
    .in28({5{1'b0}}), .in29({5{1'b0}}), .in30({5{1'b0}}), .in31({5{1'b0}}), .out(multiplexer_1_out),
    .sel(Instruction[4:0]));
  Multiplexer #(.enable("false"), .select(5), .width(5)) multiplexer_2 (
    .in0(5'b00001), .in1({5{1'b0}}), .in2(5'b00010), .in3({5{1'b0}}), .in4(5'b01011), .in5(5'b01100),
    .in6(5'b01110), .in7(5'b01101), .in8({5{1'b0}}), .in9({5{1'b0}}), .in10(5'b01000), .in11({5{1'b0}}),
    .in12({5{1'b0}}), .in13({5{1'b0}}), .in14({5{1'b0}}), .in15({5{1'b0}}), .in16({5{1'b0}}),
    .in17({5{1'b0}}), .in18({5{1'b0}}), .in19({5{1'b0}}), .in20({5{1'b0}}), .in21({5{1'b0}}),
    .in22({5{1'b0}}), .in23({5{1'b0}}), .in24({5{1'b0}}), .in25({5{1'b0}}), .in26({5{1'b0}}),
    .in27({5{1'b0}}), .in28({5{1'b0}}), .in29({5{1'b0}}), .in30({5{1'b0}}), .in31({5{1'b0}}),
    .out(multiplexer_2_out), .sel(Instruction[4:0]));
  Multiplexer #(.enable("false"), .width(5)) multiplexer_3 (
    .in0(multiplexer_1_out), .in1(multiplexer_2_out), .out(multiplexer_3_out), .sel(Instruction[5]));
  Multiplexer #(.enable("false"), .select(5), .width(5)) multiplexer_4 (
    .in0({5{1'b0}}), .in1({5{1'b0}}), .in2({5{1'b0}}), .in3({5{1'b0}}), .in4({5{1'b0}}), .in5({5{1'b0}}),
    .in6({5{1'b0}}), .in7({5{1'b0}}), .in8(5'b00001), .in9({5{1'b0}}), .in10({5{1'b0}}), .in11({5{1'b0}}),
    .in12(5'b01011), .in13(5'b01100), .in14(5'b01110), .in15({5{1'b0}}), .in16({5{1'b0}}), .in17({5{1'b0}}),
    .in18({5{1'b0}}), .in19({5{1'b0}}), .in20({5{1'b0}}), .in21({5{1'b0}}), .in22({5{1'b0}}),
    .in23({5{1'b0}}), .in24({5{1'b0}}), .in25({5{1'b0}}), .in26({5{1'b0}}), .in27({5{1'b0}}),
    .in28({5{1'b0}}), .in29({5{1'b0}}), .in30({5{1'b0}}), .in31({5{1'b0}}), .out(multiplexer_4_out),
    .sel(Instruction[30:26]));
  Multiplexer #(.enable("false"), .select(5), .width(5)) multiplexer_5 (
    .in0({5{1'b0}}), .in1({5{1'b0}}), .in2({5{1'b0}}), .in3(5'b00001), .in4({5{1'b0}}), .in5({5{1'b0}}),
    .in6({5{1'b0}}), .in7({5{1'b0}}), .in8({5{1'b0}}), .in9({5{1'b0}}), .in10({5{1'b0}}), .in11(5'b00001),
    .in12({5{1'b0}}), .in13({5{1'b0}}), .in14({5{1'b0}}), .in15({5{1'b0}}), .in16({5{1'b0}}),
    .in17({5{1'b0}}), .in18({5{1'b0}}), .in19({5{1'b0}}), .in20({5{1'b0}}), .in21({5{1'b0}}),
    .in22({5{1'b0}}), .in23({5{1'b0}}), .in24({5{1'b0}}), .in25({5{1'b0}}), .in26({5{1'b0}}),
    .in27({5{1'b0}}), .in28({5{1'b0}}), .in29({5{1'b0}}), .in30({5{1'b0}}), .in31({5{1'b0}}),
    .out(multiplexer_5_out), .sel(Instruction[30:26]));
  Multiplexer #(.enable("false"), .width(5)) multiplexer_6 (
    .in0(multiplexer_4_out), .in1(multiplexer_5_out), .out(multiplexer_6_out), .sel(Instruction[31]));
  getimmselect getimmselect_1 (.instruction(Instruction), .imm_select(getimmselect_1_imm_select));
  Multiplexer #(.enable("false"), .width(5)) multiplexer_7 (
    .in0(multiplexer_3_out), .in1(multiplexer_6_out), .out(alu_select), .sel(getimmselect_1_imm_select));
endmodule

module getrs (
  input  [31:0] Instruction,
  output [4:0] rs_select
);

  wire and_1_out, comparator_1_eq, comparator_2_eq, comparator_3_eq, or_1_out;

  Comparator #(.width(6)) comparator_1 (.a(6'b000010), .b(Instruction[5:0]), .eq(comparator_1_eq));  // open: gt, lt
  Comparator #(.width(6)) comparator_2 (.a({6{1'b0}}), .b(Instruction[5:0]), .eq(comparator_2_eq));  // open: gt, lt
  Comparator #(.width(6)) comparator_3 (.a(Instruction[31:26]), .b({6{1'b0}}), .eq(comparator_3_eq));  // open: gt, lt
  and and_1 (and_1_out, or_1_out, comparator_3_eq);
  or or_1 (or_1_out, comparator_1_eq, comparator_2_eq);
  Multiplexer #(.enable("false"), .width(5)) multiplexer_1 (
    .in0(Instruction[25:21]), .in1(Instruction[20:16]), .out(rs_select), .sel(and_1_out));
endmodule

module getrt (
  input  [31:0] Instruction,
  output [4:0] rt_select
);


  assign rt_select = Instruction[20:16];
endmodule

module getrd (
  input  [31:0] Instruction,
  output [4:0] rd_select
);

  wire [1:0] multiplexer_1_out, multiplexer_2_out, multiplexer_3_out;

  Multiplexer #(.enable("false"), .select(5), .width(2)) multiplexer_1 (
    .in0(2'b00), .in1(2'b00), .in2(2'b00), .in3(2'b10), .in4(2'b00), .in5(2'b00), .in6(2'b00), .in7(2'b00),
    .in8(2'b01), .in9(2'b00), .in10(2'b00), .in11(2'b00), .in12(2'b01), .in13(2'b01), .in14(2'b01),
    .in15(2'b00), .in16(2'b00), .in17(2'b00), .in18(2'b00), .in19(2'b00), .in20(2'b00), .in21(2'b00),
    .in22(2'b00), .in23(2'b00), .in24(2'b00), .in25(2'b00), .in26(2'b00), .in27(2'b00), .in28(2'b00),
    .in29(2'b00), .in30(2'b00), .in31(2'b00), .out(multiplexer_1_out), .sel(Instruction[30:26]));
  Multiplexer #(.enable("false"), .select(5), .width(2)) multiplexer_2 (
    .in0(2'b00), .in1(2'b00), .in2(2'b00), .in3(2'b01), .in4(2'b00), .in5(2'b00), .in6(2'b00), .in7(2'b00),
    .in8(2'b00), .in9(2'b00), .in10(2'b00), .in11(2'b00), .in12(2'b00), .in13(2'b00), .in14(2'b00),
    .in15(2'b00), .in16(2'b00), .in17(2'b00), .in18(2'b00), .in19(2'b00), .in20(2'b00), .in21(2'b00),
    .in22(2'b00), .in23(2'b00), .in24(2'b00), .in25(2'b00), .in26(2'b00), .in27(2'b00), .in28(2'b00),
    .in29(2'b00), .in30(2'b00), .in31(2'b00), .out(multiplexer_2_out), .sel(Instruction[30:26]));
  Multiplexer #(.enable("false"), .width(2)) multiplexer_3 (
    .in0(multiplexer_1_out), .in1(multiplexer_2_out), .out(multiplexer_3_out), .sel(Instruction[31]));
  Multiplexer #(.enable("false"), .select(2), .width(5)) multiplexer_4 (
    .in0(Instruction[15:11]), .in1(Instruction[20:16]), .in2({5{1'b1}}), .out(rd_select),
    .sel(multiplexer_3_out));  // open: in3

  // Notes on the sheet:
  //   rd stores our rd
  //   rt stores our rd (just for addi)
endmodule

module getwereg (
  input  [31:0] Instruction,
  output we
);

  wire comparator_1_eq, getjalselect_1_write_jumporreg, multiplexer_1_out, or_1_out;
  wire [4:0] getaluselect_1_alu_select;

  getaluselect getaluselect_1 (.Instruction(Instruction), .alu_select(getaluselect_1_alu_select));
  Comparator #(.width(6)) comparator_1 (.a(6'b101011), .b(Instruction[31:26]), .eq(comparator_1_eq));  // open: gt, lt
  getJalSelect getjalselect_1 (.Instruction(Instruction), .write_jumpOrReg(getjalselect_1_write_jumporreg));
  or or_1 (or_1_out, multiplexer_1_out, getjalselect_1_write_jumporreg);
  Multiplexer #(.enable("false"), .select(5)) multiplexer_1 (
    .in0(1'b0), .in1(1'b1), .in2(1'b1), .in3(1'b0), .in4(1'b0), .in5(1'b1), .in6(1'b1), .in7(1'b0),
    .in8(1'b1), .in9(1'b1), .in10(1'b1), .in11(1'b1), .in12(1'b1), .in13(1'b1), .in14(1'b1), .in15(1'b0),
    .in16(1'b0), .in17(1'b0), .in18(1'b0), .in19(1'b0), .in20(1'b0), .in21(1'b0), .in22(1'b0), .in23(1'b0),
    .in24(1'b0), .in25(1'b0), .in26(1'b0), .in27(1'b0), .in28(1'b0), .in29(1'b0), .in30(1'b0), .in31(1'b0),
    .out(multiplexer_1_out), .sel(getaluselect_1_alu_select));
  Multiplexer #(.enable("false")) multiplexer_2 (.in0(or_1_out), .in1(1'b0), .out(we), .sel(comparator_1_eq));
endmodule

module Control (
  input  [31:0] Instruction,
  output [4:0] rd_select,
  output [4:0] rt_select,
  output [4:0] rs_select,
  output [4:0] alu_select,
  output [4:0] shiftamt,
  output imm_select,
  output [15:0] immediate,
  output wereg,
  output wesw,
  output welw,
  output jalselect
);

  getrd getrd_1 (.Instruction(Instruction), .rd_select(rd_select));
  getrt getrt_1 (.Instruction(Instruction), .rt_select(rt_select));
  getrs getrs_1 (.Instruction(Instruction), .rs_select(rs_select));
  getaluselect getaluselect_1 (.Instruction(Instruction), .alu_select(alu_select));
  getshtamt getshtamt_1 (.Instruction(Instruction), .shiftamt(shiftamt));
  getimmselect getimmselect_1 (.instruction(Instruction), .imm_select(imm_select));
  getimm getimm_1 (.Instruction(Instruction), .immediate(immediate));
  getwereg getwereg_1 (.Instruction(Instruction), .we(wereg));
  getwesw getwesw_1 (.Instruction(Instruction), .wesw(wesw));
  getwelw getwelw_1 (.Instruction(Instruction), .welw(welw));
  getJalSelect getjalselect_1 (.Instruction(Instruction), .write_jumpOrReg(jalselect));
endmodule

module InstructionHandling (
  input  [31:0] jumpReg,
  input  IsRegEqual,
  output [31:0] InstructionOut,
  output [31:0] JumpRd
);

  wire clock_1_out, comparator_1_eq, getwrite_addorjump_1_write_addorjump,
       getwrite_addoroffset_1_write_addoroffset, getwrite_jumporreg_1_write_jumporreg;
  wire [15:0] bit_extender_2_out, bit_extender_3_out;
  wire [25:0] shifter_2_out;
  wire [31:0] adder_2_out, bit_extender_1_out, multiplexer_1_out, multiplexer_2_out, multiplexer_3_out, PC_q,
       rom_1_data, shifter_1_out;
  wire [31:16] bit_extender_3_out_2;

  assign bit_extender_1_out = {{16{bit_extender_3_out[15]}}, bit_extender_3_out};  // Bit_Extender bit_extender_1
  Adder #(.width(32)) adder_1 (.a(32'h4), .b(PC_q), .out(JumpRd));  // open: cin, cout
  getwrite_addOrOffset getwrite_addoroffset_1 (
    .Instruction(InstructionOut), .IsRegEqual(IsRegEqual),
    .write_addOrOffset(getwrite_addoroffset_1_write_addoroffset));
  Adder #(.width(32)) adder_2 (.a(bit_extender_1_out), .b(JumpRd), .out(adder_2_out));  // open: cin, cout
  Multiplexer #(.enable("false"), .width(32)) multiplexer_1 (
    .in0({bit_extender_3_out_2, bit_extender_3_out}), .in1(jumpReg), .out(multiplexer_1_out),
    .sel(getwrite_jumporreg_1_write_jumporreg));
  Multiplexer #(.enable("false"), .width(32)) multiplexer_2 (
    .in0(JumpRd), .in1(adder_2_out), .out(multiplexer_2_out), .sel(getwrite_addoroffset_1_write_addoroffset));
  Multiplexer #(.enable("false"), .width(32)) multiplexer_3 (
    .in0(multiplexer_2_out), .in1(multiplexer_1_out), .out(multiplexer_3_out),
    .sel(getwrite_addorjump_1_write_addorjump));
  Register #(.width(32)) PC (.D(multiplexer_3_out), .en(1'b1), .clk(clock_1_out), .Q(PC_q));  // open: clr
  Clock clock_1 (.out(clock_1_out));
  getwrite_JumpOrReg getwrite_jumporreg_1 (
    .Instruction(InstructionOut), .write_jumpOrReg(getwrite_jumporreg_1_write_jumporreg));
  getwrite_addOrJump getwrite_addorjump_1 (
    .Instruction(InstructionOut), .write_addOrJump(getwrite_addorjump_1_write_addorjump));
  Shifter #(.shift("lr"), .width(32)) shifter_1 (.in(PC_q), .\dist (5'b00010), .out(shifter_1_out));
  Bit_Extender #(.in_width(32)) bit_extender_2 (.in(shifter_1_out), .out(bit_extender_2_out));
  ROM #(.addrWidth(16), .dataWidth(32)) rom_1 (.addr(bit_extender_2_out), .data(rom_1_data));
  Shifter #(.width(26)) shifter_2 (.in(InstructionOut[25:0]), .\dist (5'b00010), .out(shifter_2_out));
  Comparator #(.width(32)) comparator_1 (.a(rom_1_data), .b(32'hc), .eq(comparator_1_eq));  // open: gt, lt
  assign {bit_extender_3_out_2, bit_extender_3_out} = {{6{shifter_2_out[25]}}, shifter_2_out};  // Bit_Extender bit_extender_3
  Multiplexer #(.enable("false"), .width(32)) multiplexer_4 (
    .in0(rom_1_data), .in1(32'hd009), .out(InstructionOut), .sel(comparator_1_eq));

  // Notes on the sheet:
  //   jumprd is the value we need to save to ra (or whatever reg we save our position at
  //   contents of rom_1 (hex, n*v repeats v):
  //   10400015 200d000a 104d0005 200d000c 104d0004 200d0012 104d0007 8000014 8000008 8c0b0040 11600002
  //   8c020050 ac000040 3400008 ac040080 ac050090 ac0600a0 20090001 ac0900b0 3400008 200c0001 8000014
  //   20090001 ac09002c 23bdc000 20100000 20110000 20120001 20130000 20140100 20150040 2002000c c 20080077
  //   14480002 20120000 2013ffff 20080061 14480002 2012ffff 20130000 20080064 14480002 20120001 20130000
  //   20080073 14480002 20120000 20130001 2128020 2338820 104180 1114020 11d4020 84080 8d0a0000 20090001
  //   11490013 200502a 11490011 215502a 20010001 2a5022 1149000d 220502a 1149000b 235502a 20010001 2a5022
  //   11490007 ad090000 20020012 102020 112820 143020 c 800001f 23bd4000 2002000a c
  //   if syscall, run jalr 0 k0 instead
endmodule

module getwrite_addOrOffset (
  input  [31:0] Instruction,
  input  IsRegEqual,
  output write_addOrOffset
);

  wire [1:0] bit_extender_1_out, multiplexer_1_out, multiplexer_2_out, multiplexer_3_out, xor_1_out;

  Multiplexer #(.enable("false"), .select(5), .width(2)) multiplexer_1 (
    .in0(2'b10), .in1(2'b10), .in2(2'b10), .in3(2'b10), .in4(2'b00), .in5(2'b01), .in6(2'b10), .in7(2'b10),
    .in8(2'b10), .in9(2'b10), .in10(2'b10), .in11(2'b10), .in12(2'b10), .in13(2'b10), .in14(2'b10),
    .in15(2'b10), .in16(2'b10), .in17(2'b10), .in18(2'b10), .in19(2'b10), .in20(2'b10), .in21(2'b10),
    .in22(2'b10), .in23(2'b10), .in24(2'b10), .in25(2'b10), .in26(2'b10), .in27(2'b10), .in28(2'b10),
    .in29(2'b10), .in30(2'b10), .in31(2'b10), .out(multiplexer_1_out), .sel(Instruction[30:26]));
  Multiplexer #(.enable("false"), .select(5), .width(2)) multiplexer_2 (
    .in0(2'b10), .in1(2'b10), .in2(2'b10), .in3(2'b10), .in4(2'b10), .in5(2'b10), .in6(2'b10), .in7(2'b10),
    .in8(2'b10), .in9(2'b10), .in10(2'b10), .in11(2'b10), .in12(2'b10), .in13(2'b10), .in14(2'b10),
    .in15(2'b10), .in16(2'b10), .in17(2'b10), .in18(2'b10), .in19(2'b10), .in20(2'b10), .in21(2'b10),
    .in22(2'b10), .in23(2'b10), .in24(2'b10), .in25(2'b10), .in26(2'b10), .in27(2'b10), .in28(2'b10),
    .in29(2'b10), .in30(2'b10), .in31(2'b10), .out(multiplexer_2_out), .sel(Instruction[30:26]));
  Multiplexer #(.enable("false"), .width(2)) multiplexer_3 (
    .in0(multiplexer_1_out), .in1(multiplexer_2_out), .out(multiplexer_3_out), .sel(Instruction[31]));
  assign bit_extender_1_out = {{1{1'b0}}, IsRegEqual};  // Bit_Extender bit_extender_1
  assign xor_1_out = multiplexer_3_out ^ bit_extender_1_out;  // XOR_Gate xor_1, 2 bits wide
  Comparator #(.width(2)) comparator_1 (.a(2'b01), .b(xor_1_out), .eq(write_addOrOffset));  // open: gt, lt
endmodule

module getwrite_addOrJump (
  input  [31:0] Instruction,
  output write_addOrJump
);

  wire and_1_out, comparator_1_eq, multiplexer_1_out, multiplexer_2_out, multiplexer_3_out,
       multiplexer_4_out, multiplexer_5_out, multiplexer_6_out;

  Multiplexer #(.enable("false"), .select(5)) multiplexer_1 (
    .in0(1'b0), .in1(1'b0), .in2(1'b1), .in3(1'b1), .in4(1'b0), .in5(1'b0), .in6(1'b0), .in7(1'b0),
    .in8(1'b0), .in9(1'b0), .in10(1'b0), .in11(1'b0), .in12(1'b0), .in13(1'b0), .in14(1'b0), .in15(1'b0),
    .in16(1'b0), .in17(1'b0), .in18(1'b0), .in19(1'b0), .in20(1'b0), .in21(1'b0), .in22(1'b0), .in23(1'b0),
    .in24(1'b0), .in25(1'b0), .in26(1'b0), .in27(1'b0), .in28(1'b0), .in29(1'b0), .in30(1'b0), .in31(1'b0),
    .out(multiplexer_1_out), .sel(Instruction[30:26]));
  Multiplexer #(.enable("false"), .select(5)) multiplexer_2 (
    .in0(1'b0), .in1(1'b0), .in2(1'b0), .in3(1'b0), .in4(1'b0), .in5(1'b0), .in6(1'b0), .in7(1'b0),
    .in8(1'b0), .in9(1'b0), .in10(1'b0), .in11(1'b0), .in12(1'b0), .in13(1'b0), .in14(1'b0), .in15(1'b0),
    .in16(1'b0), .in17(1'b0), .in18(1'b0), .in19(1'b0), .in20(1'b0), .in21(1'b0), .in22(1'b0), .in23(1'b0),
    .in24(1'b0), .in25(1'b0), .in26(1'b0), .in27(1'b0), .in28(1'b0), .in29(1'b0), .in30(1'b0), .in31(1'b0),
    .out(multiplexer_2_out), .sel(Instruction[30:26]));
  Comparator #(.width(6)) comparator_1 (.a({6{1'b0}}), .b(Instruction[31:26]), .eq(comparator_1_eq));  // open: gt, lt
  Multiplexer #(.enable("false")) multiplexer_3 (
    .in0(multiplexer_1_out), .in1(multiplexer_2_out), .out(multiplexer_3_out), .sel(Instruction[31]));
  Multiplexer #(.enable("false"), .select(5)) multiplexer_4 (
    .in0(1'b0), .in1(1'b0), .in2(1'b0), .in3(1'b0), .in4(1'b0), .in5(1'b0), .in6(1'b0), .in7(1'b0),
    .in8(1'b1), .in9(1'b1), .in10(1'b0), .in11(1'b0), .in12(1'b0), .in13(1'b0), .in14(1'b0), .in15(1'b0),
    .in16(1'b0), .in17(1'b0), .in18(1'b0), .in19(1'b0), .in20(1'b0), .in21(1'b0), .in22(1'b0), .in23(1'b0),
    .in24(1'b0), .in25(1'b0), .in26(1'b0), .in27(1'b0), .in28(1'b0), .in29(1'b0), .in30(1'b0), .in31(1'b0),
    .out(multiplexer_4_out), .sel(Instruction[4:0]));
  Multiplexer #(.enable("false"), .select(5)) multiplexer_5 (
    .in0(1'b0), .in1(1'b0), .in2(1'b0), .in3(1'b0), .in4(1'b0), .in5(1'b0), .in6(1'b0), .in7(1'b0),
    .in8(1'b0), .in9(1'b0), .in10(1'b0), .in11(1'b0), .in12(1'b0), .in13(1'b0), .in14(1'b0), .in15(1'b0),
    .in16(1'b0), .in17(1'b0), .in18(1'b0), .in19(1'b0), .in20(1'b0), .in21(1'b0), .in22(1'b0), .in23(1'b0),
    .in24(1'b0), .in25(1'b0), .in26(1'b0), .in27(1'b0), .in28(1'b0), .in29(1'b0), .in30(1'b0), .in31(1'b0),
    .out(multiplexer_5_out), .sel(Instruction[4:0]));
  Multiplexer #(.enable("false")) multiplexer_6 (
    .in0(multiplexer_4_out), .in1(multiplexer_5_out), .out(multiplexer_6_out), .sel(Instruction[5]));
  and and_1 (and_1_out, multiplexer_6_out, comparator_1_eq);
  or or_1 (write_addOrJump, multiplexer_3_out, and_1_out);
endmodule

module getwrite_JumpOrReg (
  input  [31:0] Instruction,
  output write_jumpOrReg
);

  wire and_1_out, comparator_1_eq, multiplexer_1_out, multiplexer_2_out, multiplexer_3_out,
       multiplexer_4_out, multiplexer_5_out, multiplexer_6_out;

  Multiplexer #(.enable("false"), .select(5)) multiplexer_1 (
    .in0(1'b0), .in1(1'b0), .in2(1'b0), .in3(1'b0), .in4(1'b0), .in5(1'b0), .in6(1'b0), .in7(1'b0),
    .in8(1'b0), .in9(1'b0), .in10(1'b0), .in11(1'b0), .in12(1'b0), .in13(1'b0), .in14(1'b0), .in15(1'b0),
    .in16(1'b0), .in17(1'b0), .in18(1'b0), .in19(1'b0), .in20(1'b0), .in21(1'b0), .in22(1'b0), .in23(1'b0),
    .in24(1'b0), .in25(1'b0), .in26(1'b0), .in27(1'b0), .in28(1'b0), .in29(1'b0), .in30(1'b0), .in31(1'b0),
    .out(multiplexer_1_out), .sel(Instruction[30:26]));
  Multiplexer #(.enable("false"), .select(5)) multiplexer_2 (
    .in0(1'b0), .in1(1'b0), .in2(1'b0), .in3(1'b0), .in4(1'b0), .in5(1'b0), .in6(1'b0), .in7(1'b0),
    .in8(1'b0), .in9(1'b0), .in10(1'b0), .in11(1'b0), .in12(1'b0), .in13(1'b0), .in14(1'b0), .in15(1'b0),
    .in16(1'b0), .in17(1'b0), .in18(1'b0), .in19(1'b0), .in20(1'b0), .in21(1'b0), .in22(1'b0), .in23(1'b0),
    .in24(1'b0), .in25(1'b0), .in26(1'b0), .in27(1'b0), .in28(1'b0), .in29(1'b0), .in30(1'b0), .in31(1'b0),
    .out(multiplexer_2_out), .sel(Instruction[30:26]));
  Comparator #(.width(6)) comparator_1 (.a({6{1'b0}}), .b(Instruction[31:26]), .eq(comparator_1_eq));  // open: gt, lt
  Multiplexer #(.enable("false")) multiplexer_3 (
    .in0(multiplexer_1_out), .in1(multiplexer_2_out), .out(multiplexer_3_out), .sel(Instruction[31]));
  Multiplexer #(.enable("false"), .select(5)) multiplexer_4 (
    .in0(1'b0), .in1(1'b0), .in2(1'b0), .in3(1'b0), .in4(1'b0), .in5(1'b0), .in6(1'b0), .in7(1'b0),
    .in8(1'b1), .in9(1'b1), .in10(1'b0), .in11(1'b0), .in12(1'b0), .in13(1'b0), .in14(1'b0), .in15(1'b0),
    .in16(1'b0), .in17(1'b0), .in18(1'b0), .in19(1'b0), .in20(1'b0), .in21(1'b0), .in22(1'b0), .in23(1'b0),
    .in24(1'b0), .in25(1'b0), .in26(1'b0), .in27(1'b0), .in28(1'b0), .in29(1'b0), .in30(1'b0), .in31(1'b0),
    .out(multiplexer_4_out), .sel(Instruction[4:0]));
  Multiplexer #(.enable("false"), .select(5)) multiplexer_5 (
    .in0(1'b0), .in1(1'b0), .in2(1'b0), .in3(1'b0), .in4(1'b0), .in5(1'b0), .in6(1'b0), .in7(1'b0),
    .in8(1'b0), .in9(1'b0), .in10(1'b0), .in11(1'b0), .in12(1'b0), .in13(1'b0), .in14(1'b0), .in15(1'b0),
    .in16(1'b0), .in17(1'b0), .in18(1'b0), .in19(1'b0), .in20(1'b0), .in21(1'b0), .in22(1'b0), .in23(1'b0),
    .in24(1'b0), .in25(1'b0), .in26(1'b0), .in27(1'b0), .in28(1'b0), .in29(1'b0), .in30(1'b0), .in31(1'b0),
    .out(multiplexer_5_out), .sel(Instruction[4:0]));
  Multiplexer #(.enable("false")) multiplexer_6 (
    .in0(multiplexer_4_out), .in1(multiplexer_5_out), .out(multiplexer_6_out), .sel(Instruction[5]));
  and and_1 (and_1_out, multiplexer_6_out, comparator_1_eq);
  or or_1 (write_jumpOrReg, multiplexer_3_out, and_1_out);
endmodule

module getwesw (
  input  [31:0] Instruction,
  output wesw
);

  Comparator #(.width(6)) comparator_1 (.a(6'b101011), .b(Instruction[31:26]), .eq(wesw));  // open: gt, lt
endmodule

module getwelw (
  input  [31:0] Instruction,
  output welw
);

  Comparator #(.width(6)) comparator_1 (.a(6'b100011), .b(Instruction[31:26]), .eq(welw));  // open: gt, lt
endmodule

module getJalSelect (
  input  [31:0] Instruction,
  output write_jumpOrReg
);

  wire and_1_out, comparator_1_eq, multiplexer_1_out, multiplexer_2_out, multiplexer_3_out,
       multiplexer_4_out, multiplexer_5_out, multiplexer_6_out;

  Multiplexer #(.enable("false"), .select(5)) multiplexer_1 (
    .in0(1'b0), .in1(1'b0), .in2(1'b0), .in3(1'b1), .in4(1'b0), .in5(1'b0), .in6(1'b0), .in7(1'b0),
    .in8(1'b0), .in9(1'b0), .in10(1'b0), .in11(1'b0), .in12(1'b0), .in13(1'b0), .in14(1'b0), .in15(1'b0),
    .in16(1'b0), .in17(1'b0), .in18(1'b0), .in19(1'b0), .in20(1'b0), .in21(1'b0), .in22(1'b0), .in23(1'b0),
    .in24(1'b0), .in25(1'b0), .in26(1'b0), .in27(1'b0), .in28(1'b0), .in29(1'b0), .in30(1'b0), .in31(1'b0),
    .out(multiplexer_1_out), .sel(Instruction[30:26]));
  Multiplexer #(.enable("false"), .select(5)) multiplexer_2 (
    .in0(1'b0), .in1(1'b0), .in2(1'b0), .in3(1'b0), .in4(1'b0), .in5(1'b0), .in6(1'b0), .in7(1'b0),
    .in8(1'b0), .in9(1'b0), .in10(1'b0), .in11(1'b0), .in12(1'b0), .in13(1'b0), .in14(1'b0), .in15(1'b0),
    .in16(1'b0), .in17(1'b0), .in18(1'b0), .in19(1'b0), .in20(1'b0), .in21(1'b0), .in22(1'b0), .in23(1'b0),
    .in24(1'b0), .in25(1'b0), .in26(1'b0), .in27(1'b0), .in28(1'b0), .in29(1'b0), .in30(1'b0), .in31(1'b0),
    .out(multiplexer_2_out), .sel(Instruction[30:26]));
  Comparator #(.width(6)) comparator_1 (.a({6{1'b0}}), .b(Instruction[31:26]), .eq(comparator_1_eq));  // open: gt, lt
  Multiplexer #(.enable("false")) multiplexer_3 (
    .in0(multiplexer_1_out), .in1(multiplexer_2_out), .out(multiplexer_3_out), .sel(Instruction[31]));
  Multiplexer #(.enable("false"), .select(5)) multiplexer_4 (
    .in0(1'b0), .in1(1'b0), .in2(1'b0), .in3(1'b0), .in4(1'b0), .in5(1'b0), .in6(1'b0), .in7(1'b0),
    .in8(1'b0), .in9(1'b1), .in10(1'b0), .in11(1'b0), .in12(1'b0), .in13(1'b0), .in14(1'b0), .in15(1'b0),
    .in16(1'b0), .in17(1'b0), .in18(1'b0), .in19(1'b0), .in20(1'b0), .in21(1'b0), .in22(1'b0), .in23(1'b0),
    .in24(1'b0), .in25(1'b0), .in26(1'b0), .in27(1'b0), .in28(1'b0), .in29(1'b0), .in30(1'b0), .in31(1'b0),
    .out(multiplexer_4_out), .sel(Instruction[4:0]));
  Multiplexer #(.enable("false"), .select(5)) multiplexer_5 (
    .in0(1'b0), .in1(1'b0), .in2(1'b0), .in3(1'b0), .in4(1'b0), .in5(1'b0), .in6(1'b0), .in7(1'b0),
    .in8(1'b0), .in9(1'b0), .in10(1'b0), .in11(1'b0), .in12(1'b0), .in13(1'b0), .in14(1'b0), .in15(1'b0),
    .in16(1'b0), .in17(1'b0), .in18(1'b0), .in19(1'b0), .in20(1'b0), .in21(1'b0), .in22(1'b0), .in23(1'b0),
    .in24(1'b0), .in25(1'b0), .in26(1'b0), .in27(1'b0), .in28(1'b0), .in29(1'b0), .in30(1'b0), .in31(1'b0),
    .out(multiplexer_5_out), .sel(Instruction[4:0]));
  Multiplexer #(.enable("false")) multiplexer_6 (
    .in0(multiplexer_4_out), .in1(multiplexer_5_out), .out(multiplexer_6_out), .sel(Instruction[5]));
  and and_1 (and_1_out, multiplexer_6_out, comparator_1_eq);
  or or_1 (write_jumpOrReg, multiplexer_3_out, and_1_out);
endmodule

module CPU (
  input  [31:0] Data_bus_in,
  output [31:0] Data_bus,
  output Data_write_e,
  output [15:0] Address,
  output Mem_write_e
);

  wire alu_1_isregequal, control_1_imm_select, control_1_jalselect, control_1_welw, control_1_wereg;
  wire [4:0] control_1_alu_select, control_1_rd_select, control_1_rs_select, control_1_rt_select,
       control_1_shiftamt;
  wire [15:0] control_1_immediate;
  wire [31:0] alu_1_outval, bit_extender_1_out, instructionhandling_1_instructionout,
       instructionhandling_1_jumprd, multiplexer_1_out, multiplexer_2_out, multiplexer_3_out, regfile_1_rs,
       shifter_1_out;

  Control control_1 (
    .Instruction(instructionhandling_1_instructionout), .rd_select(control_1_rd_select),
    .rt_select(control_1_rt_select), .rs_select(control_1_rs_select), .alu_select(control_1_alu_select),
    .shiftamt(control_1_shiftamt), .imm_select(control_1_imm_select), .immediate(control_1_immediate),
    .wereg(control_1_wereg), .wesw(Data_write_e), .welw(control_1_welw), .jalselect(control_1_jalselect));
  InstructionHandling instructionhandling_1 (
    .jumpReg(regfile_1_rs), .IsRegEqual(alu_1_isregequal),
    .InstructionOut(instructionhandling_1_instructionout), .JumpRd(instructionhandling_1_jumprd));
  Multiplexer #(.enable("false"), .width(32)) multiplexer_1 (
    .in0(multiplexer_3_out), .in1(instructionhandling_1_jumprd), .out(multiplexer_1_out),
    .sel(control_1_jalselect));
  assign bit_extender_1_out = {{16{control_1_immediate[15]}}, control_1_immediate};  // Bit_Extender bit_extender_1
  regfile regfile_1 (
    .we(control_1_wereg), .rdselect(control_1_rd_select), .rd(multiplexer_1_out),
    .rsselect(control_1_rs_select), .rtselect(control_1_rt_select), .rt(Data_bus), .rs(regfile_1_rs));
  Multiplexer #(.enable("false"), .width(32)) multiplexer_2 (
    .in0(Data_bus), .in1(bit_extender_1_out), .out(multiplexer_2_out), .sel(control_1_imm_select));
  Multiplexer #(.enable("false"), .width(32)) multiplexer_3 (
    .in0(alu_1_outval), .in1(Data_bus_in), .out(multiplexer_3_out), .sel(control_1_welw));
  ALU alu_1 (
    .arith_code(control_1_alu_select), .IN1(regfile_1_rs), .IN2(multiplexer_2_out),
    .shift_amt(control_1_shiftamt), .isRegEqual(alu_1_isregequal), .outval(alu_1_outval));
  Shifter #(.shift("lr"), .width(32)) shifter_1 (.in(alu_1_outval), .\dist (5'b00010), .out(shifter_1_out));
  Bit_Extender #(.in_width(32)) bit_extender_2 (.in(shifter_1_out), .out(Address));

  assign Mem_write_e = Data_write_e;
endmodule

module RGBController (
  input  [15:0] AddressIn,
  input  [31:0] DataBusIn,
  input  WriteEnable,
  output [5:0] RGBX,
  output [5:0] RGBY,
  output [23:0] RGBColor,
  output RGBWrite
);

  wire and_1_out, and_2_out, and_3_out, clock_1_out, comparator_1_eq, comparator_2_eq, comparator_3_eq,
       comparator_4_eq, comparator_5_eq;
  wire [31:0] RGB_q, x_coordinate_q, y_coordinate_q;

  Comparator #(.width(1)) comparator_1 (.a(1'b1), .b(WriteEnable), .eq(comparator_1_eq));  // open: gt, lt
  Comparator #(.width(16)) comparator_2 (.a(16'h20), .b(AddressIn), .eq(comparator_2_eq));  // open: gt, lt
  Comparator #(.width(16)) comparator_3 (.a(16'h24), .b(AddressIn), .eq(comparator_3_eq));  // open: gt, lt
  Comparator #(.width(16)) comparator_4 (.a(16'h28), .b(AddressIn), .eq(comparator_4_eq));  // open: gt, lt
  Comparator #(.width(16)) comparator_5 (.a(16'h2c), .b(AddressIn), .eq(comparator_5_eq));  // open: gt, lt
  and and_1 (and_1_out, comparator_2_eq, comparator_1_eq);
  and and_2 (and_2_out, comparator_3_eq, comparator_1_eq);
  and and_3 (and_3_out, comparator_4_eq, comparator_1_eq);
  and and_4 (RGBWrite, comparator_5_eq, comparator_1_eq);
  Clock clock_1 (.out(clock_1_out));
  Register #(.width(32)) x_coordinate (
    .D(DataBusIn), .en(and_1_out), .clk(clock_1_out), .Q(x_coordinate_q));  // open: clr
  Register #(.width(32)) y_coordinate (
    .D(DataBusIn), .en(and_2_out), .clk(clock_1_out), .Q(y_coordinate_q));  // open: clr
  Register #(.width(32)) RGB (.D(DataBusIn), .en(and_3_out), .clk(clock_1_out), .Q(RGB_q));  // open: clr
  Bit_Extender #(.in_width(32), .out_width(6), .\type ("zero")) bit_extender_1 (.in(x_coordinate_q), .out(RGBX));
  Bit_Extender #(.in_width(32), .out_width(24), .\type ("zero")) bit_extender_2 (.in(RGB_q), .out(RGBColor));
  Bit_Extender #(.in_width(32), .out_width(6), .\type ("zero")) bit_extender_3 (.in(y_coordinate_q), .out(RGBY));
endmodule

module KeyboardController (
  input  [31:0] DataBusIn,
  input  WriteEnable,
  input  [15:0] AddressIn,
  input  [6:0] KeyboardIn,
  input  KeyboardKeyPressAvailable,
  output [31:0] DataBusOut,
  output DataBusWrite,
  output KeyboardRead
);

  wire and_2_out, and_3_out, comparator_1_eq, comparator_1_lt, comparator_2_eq, comparator_3_eq,
       comparator_4_eq;
  wire [31:0] bit_extender_1_out, bit_extender_2_out;

  Comparator #(.width(1)) comparator_1 (
    .a(1'b1), .b(WriteEnable), .eq(comparator_1_eq), .lt(comparator_1_lt));  // open: gt
  Comparator #(.width(16)) comparator_2 (.a(16'h10), .b(AddressIn), .eq(comparator_2_eq));  // open: gt, lt
  Comparator #(.width(32)) comparator_3 (.a({32{1'b0}}), .b(DataBusIn), .eq(comparator_3_eq));  // open: gt, lt
  Comparator #(.width(16)) comparator_4 (.a(16'h14), .b(AddressIn), .eq(comparator_4_eq));  // open: gt, lt
  and and_1 (KeyboardRead, comparator_1_eq, comparator_2_eq, comparator_3_eq);
  and and_2 (and_2_out, comparator_1_lt, comparator_4_eq);
  and and_3 (and_3_out, comparator_1_lt, comparator_2_eq, KeyboardKeyPressAvailable);
  assign bit_extender_1_out = {{25{1'b0}}, KeyboardIn};  // Bit_Extender bit_extender_1
  or or_1 (DataBusWrite, comparator_4_eq, comparator_2_eq);
  assign bit_extender_2_out = {{31{1'b0}}, and_3_out};  // Bit_Extender bit_extender_2
  Multiplexer #(.enable("false"), .width(32)) multiplexer_1 (
    .in0(bit_extender_2_out), .in1(bit_extender_1_out), .out(DataBusOut), .sel(and_2_out));
endmodule

module Memory (
  input  Write_e,
  input  [15:0] Address,
  input  [31:0] Data_Bus_in,
  output [31:0] Data_Bus_out,
  output Data_Bus_Write_e
);

  wire clock_1_out, comparator_1_eq, multiplexer_1_out, not_1_out, not_2_out, not_3_out;

  Comparator comparator_1 (.a({8{1'b0}}), .b(Address[15:8]), .eq(comparator_1_eq));  // open: gt, lt
  not not_1 (not_1_out, Write_e);
  not not_2 (not_2_out, comparator_1_eq);
  not not_3 (not_3_out, comparator_1_eq);
  and and_1 (Data_Bus_Write_e, not_1_out, not_2_out);
  Multiplexer #(.enable("false")) multiplexer_1 (
    .in0(Write_e), .in1(not_3_out), .out(multiplexer_1_out), .sel(comparator_1_eq));
  Clock clock_1 (.out(clock_1_out));
  RAM #(.addrWidth(16), .dataWidth(32), .enables("line")) ram_1 (
    .addr(Address), .we(multiplexer_1_out), .clk(clock_1_out), .din(Data_Bus_in), .dout(Data_Bus_out));

  // Notes on the sheet:
  //   More logic needed to determine WHEN you read/writing from mem and when you need to write to the bus
endmodule
